# Fritzing sketch SmartWatt Fritzing V2 (saved by Fritzing 0.9.5d)

parts:
  esp1 = ESP32 DevKitc V4
  RY1 = SSR-40VA
  Part8 = ACS712 Current Sensor 5A 20A 30A
  R1 = Resistor [tolerance=±5% resistance=220 package=THT]
  R2 = Resistor [tolerance=±5% resistance=1k package=THT]
  OLED_I2C1 = OLED 128x64 I2C Monochrome Display
  S1 = SWITCH-MOMENTARY-2 [package=reed_switch_pth]
  S2 = SWITCH-MOMENTARY-2 [package=reed_switch_pth]

nets:
  N1: esp1.IO18, S2.1
  N2: esp1.IO19, S1.1
  N3: esp1.IO21, OLED_I2C1.SDA
  N4: esp1.IO22, OLED_I2C1.SCK
  N5: esp1.GND, RY1.Pin_4, S2.2
  N6: esp1.IO34, Part8.2, Part8.OUT
  N7: esp1.IO33, RY1.Pin_3
  N8: esp1.CMD, Part8.GND, R2.Pin_1
  5V: esp1.5V, Part8.VCC, R1.Pin_0, OLED_I2C1.VDD
  N9: RY1.Pin_1, Part8.1
  N10: R1.Pin_1, R2.Pin_0
  N11: OLED_I2C1.GND, S1.2

custom parts:
  ESP32 DevKitc V4: ESP32-DevKitC board with ESP32-WROOM-32 module. ESP32-DevKitC V4 is a small-sized ESP32-based development board produced by Espressif. Most of the pins on the ESP module are broken out to the pin headers on the board. The pins D0, D1, D2, D3, CMD and CLK are used internally for communication between ESP32 and SPI flash memory. They are grouped on both sides near the USB connector. Avoid using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
  SSR-40VA: SSR-40VA solid state relay.
  ACS712 Current Sensor 5A 20A 30A: Remix by Michael Kubina http://www.kubina.info Original by: https://forum.fritzing.org/t/current-sensor-5a-acs712/7694 https://forum.fritzing.org/u/ArtHome ArtHome12@gmail.com
