# Fritzing sketch SmartWatt (saved by Fritzing 0.9.5d)

parts:
  esp1 = ESP32 DevKitc V4
  RY1 = SSR-40VA
  Part2 = ACS712 Current Sensor 5A 20A 30A
  Part3 = Arduino Nano (Rev3.0)
  Part4 = NRF24L01+ Breakout Board
  Part5 = ACS712 Current Sensor 5A 20A 30A
  Part6 = Arduino Nano (Rev3.0)
  Part7 = NRF24L01+ Breakout Board
  Part8 = ACS712 Current Sensor 5A 20A 30A
  Part9 = Arduino Nano (Rev3.0)
  Part10 = NRF24L01+ Breakout Board
  Part11 = NRF24L01+ Breakout Board

nets:
  N1: esp1.IO4, Part11.CE
  N2: esp1.IO5, Part11.CS
  N3: esp1.IO18, Part11.SCK
  N4: esp1.IO19, Part11.MISO
  N5: esp1.IO21, RY1.Pin_3
  N6: esp1.IO23, Part11.MOSI
  GND: esp1.GND, RY1.Pin_4, Part11.GND
  3V3: esp1.3V3, Part11.VCC
  N7: Part2.2, Part2.OUT, Part3.RESET
  VCC: Part2.VCC, Part3.5V
  GND_2: Part2.GND, Part3.GND, Part4.GND
  N8: Part3.D9, Part4.CE
  N9: Part3.D10, Part4.CS
  N10: Part3.D11/MOSI, Part4.MOSI
  N11: Part3.D12/MISO, Part4.MISO
  3V3_2: Part3.3V3, Part4.VCC
  N12: Part3.D13/SCK, Part4.SCK
  N13: Part5.2, Part5.OUT, Part6.RESET
  VCC_2: Part5.VCC, Part6.5V
  GND_3: Part5.GND, Part6.GND, Part7.GND
  N14: Part6.D9, Part7.CE
  N15: Part6.D10, Part7.CS
  N16: Part6.D11/MOSI, Part7.MOSI
  N17: Part6.D12/MISO, Part7.MISO
  3V3_3: Part6.3V3, Part7.VCC
  N18: Part6.D13/SCK, Part7.SCK
  N19: Part8.2, Part8.OUT, Part9.RESET
  VCC_3: Part8.VCC, Part9.5V
  GND_4: Part8.GND, Part9.GND, Part10.GND
  N20: Part9.D9, Part10.CE
  N21: Part9.D10, Part10.CS
  N22: Part9.D11/MOSI, Part10.MOSI
  N23: Part9.D12/MISO, Part10.MISO
  3V3_4: Part9.3V3, Part10.VCC
  N24: Part9.D13/SCK, Part10.SCK

custom parts:
  ESP32 DevKitc V4: ESP32-DevKitC board with ESP32-WROOM-32 module. ESP32-DevKitC V4 is a small-sized ESP32-based development board produced by Espressif. Most of the pins on the ESP module are broken out to the pin headers on the board. The pins D0, D1, D2, D3, CMD and CLK are used internally for communication between ESP32 and SPI flash memory. They are grouped on both sides near the USB connector. Avoid using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
  SSR-40VA: SSR-40VA solid state relay.
  ACS712 Current Sensor 5A 20A 30A: Remix by Michael Kubina http://www.kubina.info Original by: https://forum.fritzing.org/t/current-sensor-5a-acs712/7694 https://forum.fritzing.org/u/ArtHome ArtHome12@gmail.com
